// Logisim project MIPS Project.circ as structural Verilog
module IM (
  input  [5:0] in_1,
  output [3:0] Shft_Amnt_0_3,
  output [3:0] Dst_reg_4_7,
  output [3:0] Src_Reg_2_8_11,
  output [3:0] Src_Reg_1_12_15,
  output [3:0] Opcode__19_16,
  output [7:0] Add_Immi_0_7,
  output [7:0] Jump_Add_8_15
);

  ROM #(.addrWidth(6), .dataWidth(20)) rom_1 (
    .addr(in_1), .data({Jump_Add_8_15[7:4], Jump_Add_8_15, Add_Immi_0_7}));  // open: sel

  assign Dst_reg_4_7 = Add_Immi_0_7[7:4];
  assign Opcode__19_16 = Jump_Add_8_15[7:4];
  assign Shft_Amnt_0_3 = Add_Immi_0_7[3:0];
  assign Src_Reg_1_12_15 = Jump_Add_8_15[7:4];
  assign Src_Reg_2_8_11 = Jump_Add_8_15[3:0];
endmodule

module Register_File (
  input  [7:0] Data,
  input  [3:0] ReadREg_1,
  input  [3:0] WriteRegister,
  input  [3:0] ReadReg_2,
  input  WriteSignal,
  output [7:0] out_6,
  output [7:0] out_7,
  output [7:0] out_8,
  output [7:0] out_9,
  output [7:0] out_10,
  output [7:0] out_11,
  output [7:0] out_12,
  output [7:0] out_13,
  output [7:0] out_14,
  output [7:0] out_15
);

  wire and_1_out, and_2_out, and_3_out, and_4_out, and_5_out, and_6_out, and_7_out, and_8_out, clock_1_out,
       decoder_1_out0, decoder_1_out1, decoder_1_out2, decoder_1_out3, decoder_1_out4, decoder_1_out5,
       decoder_1_out6, decoder_1_out7;

  Decoder #(.select(4)) decoder_1 (
    .out0(decoder_1_out0), .out1(decoder_1_out1), .out2(decoder_1_out2), .out3(decoder_1_out3),
    .out4(decoder_1_out4), .out5(decoder_1_out5), .out6(decoder_1_out6), .out7(decoder_1_out7),
    .sel(WriteRegister));  // open: out8, out9, out10, out11, out12, out13, out14, out15, en
  and and_1 (and_1_out, decoder_1_out0, 1'b0);
  and and_2 (and_2_out, decoder_1_out1, WriteSignal);
  and and_3 (and_3_out, decoder_1_out2, WriteSignal);
  and and_4 (and_4_out, decoder_1_out3, WriteSignal);
  and and_5 (and_5_out, decoder_1_out4, WriteSignal);
  and and_6 (and_6_out, decoder_1_out5, WriteSignal);
  and and_7 (and_7_out, decoder_1_out6, WriteSignal);
  and and_8 (and_8_out, decoder_1_out7, WriteSignal);
  Clock clock_1 (.out(clock_1_out));
  Register register_1 (.D(Data), .en(and_1_out), .Q(out_12), .clk(clock_1_out));  // open: clr
  Register register_2 (.D(Data), .en(and_2_out), .Q(out_13), .clk(clock_1_out));  // open: clr
  Register register_3 (.D(Data), .en(and_3_out), .Q(out_14), .clk(clock_1_out));  // open: clr
  Register register_4 (.D(Data), .en(and_4_out), .Q(out_15), .clk(clock_1_out));  // open: clr
  Register register_5 (.D(Data), .en(and_5_out), .Q(out_11), .clk(clock_1_out));  // open: clr
  Register register_6 (.D(Data), .en(and_6_out), .Q(out_10), .clk(clock_1_out));  // open: clr
  Register register_7 (.D(Data), .en(and_7_out), .Q(out_9), .clk(clock_1_out));  // open: clr
  Register register_8 (.D(Data), .en(and_8_out), .Q(out_8), .clk(clock_1_out));  // open: clr
  Multiplexer #(.select(4), .width(8)) multiplexer_1 (
    .in0(out_12), .in1(out_13), .in2(out_14), .in3(out_15), .in4(out_11), .in5(out_10), .in6(out_9),
    .in7(out_8), .out(out_6), .sel(ReadREg_1));  // open: in8, in9, in10, in11, in12, in13, in14, in15, en
  Multiplexer #(.select(4), .width(8)) multiplexer_2 (
    .in0(out_12), .in1(out_13), .in2(out_14), .in3(out_15), .in4(out_11), .in5(out_10), .in6(out_9),
    .in7(out_8), .out(out_7), .sel(ReadReg_2));  // open: in8, in9, in10, in11, in12, in13, in14, in15, en

  // Notes on the sheet:
  //   CLK
  //   Zero
  //   t0
  //   t1
  //   t2
  //   Zero
  //   t0
  //   t1
  //   t2
  //   t3
  //   t4
  //   t5
  //   SP
  //   t3
  //   t4
  //   t5
  //   SP
  //   ReadData-1
  //   ReadData-2
endmodule
